# Fritzing sketch RPi_fan_ctrl (saved by Fritzing 0.9.3b)
breadboards: 1

parts:
  M1 = DC Motor
  Raspberry_Pi_1 = Raspberry Pi 3 [part_number=RPI-3-V1.2]
  D1 = Rectifier Diode [part_number=1N4001 package="Melf DO-213 AB [SMD]"]
  Q1 = TRANSISTOR_NPN [package=to-92]
  R1 = Resistor [tolerance=±5% resistance=1k package=THT]

nets:
  N1: M1.pin_1, Raspberry_Pi_1.5V, D1.cathode
  N2: M1.pin_2, D1.anode, Q1.C
  N3: Raspberry_Pi_1.GND, Q1.E
  N4: Raspberry_Pi_1.GIPO18, R1.Pin_0
  N5: Q1.B, R1.Pin_1
