# Fritzing sketch RPi_fan_ctrl_2 (saved by Fritzing 0.9.3b)
stripboards: 1

parts:
  D1 = Rectifier Diode [part_number=1N4001 package="300 mil [THT]"]
  Raspberry_Pi_1 = Raspberry Pi 3 [part_number=RPI-3-V1.2]
  R1 = Resistor [tolerance=±5% resistance=10 package=THT]
  R2 = Resistor [tolerance=±5% resistance=1k package=THT]
  C1 = Electrolytic Capacitor [capacitance=330µF voltage=16V package="100 mil [THT, electrolytic]"]
  Q1 = NPN-Transistor [part_number=1N2222 package="TO92 [THT]"]
  M1 = DC Motor

nets:
  N1: D1.cathode, R1.Pin_1, C1.+, M1.pin_1
  N2: D1.anode, Q1.C, M1.pin_2
  N3: Raspberry_Pi_1.GND, C1.-, Q1.E
  N4: Raspberry_Pi_1.GPIO18, R2.Pin_0
  N5: Raspberry_Pi_1.5V, R1.Pin_0
  N6: R2.Pin_1, Q1.B

notes:
  Current limiter: 500mA
  Small energy buffer to smoothen the load on the 5V supply.
